// Logisim project hw2_q2.circ as structural Verilog
module F (
  input  A,
  input  B,
  input  C,
  input  D,
  output out_5
);

  wire nand_1_out, nand_2_out, nand_3_out, nand_4_out, nand_5_out, nand_6_out, nand_7_out;

  nand nand_1 (nand_1_out, A, A);
  nand nand_2 (nand_2_out, B, B);
  nand nand_3 (nand_3_out, D, D);
  nand nand_4 (nand_4_out, A, nand_2_out);
  nand nand_5 (nand_5_out, A, D);
  nand nand_6 (nand_6_out, C, B);
  nand nand_7 (nand_7_out, nand_1_out, nand_2_out, nand_3_out);
  nand nand_8 (out_5, nand_4_out, nand_5_out, nand_6_out, nand_7_out);
endmodule

module F_2 (
  input  A,
  input  B,
  input  C,
  input  D,
  output out_5
);

  wire nand_1_out, nand_2_out, nand_3_out, nand_4_out, nand_5_out, nand_6_out, nand_7_out;

  nand nand_1 (nand_1_out, A, A);
  nand nand_2 (nand_2_out, B, B);
  nand nand_3 (nand_3_out, C, C);
  nand nand_4 (nand_4_out, D, D);
  nand nand_5 (nand_5_out, nand_1_out, nand_2_out, D);
  nand nand_6 (nand_6_out, nand_1_out, B, nand_3_out);
  nand nand_7 (nand_7_out, B, nand_3_out, nand_4_out);
  nand nand_8 (out_5, nand_5_out, nand_6_out, nand_7_out);
endmodule
