// Logisim project hw3_controller.circ as structural Verilog: 1 circuit, main circuit main
module main (
  input  a,
  output x,
  output y,
  output z
);

  wire and_1_out, and_2_out, and_3_out, and_4_out, and_5_out, and_6_out, and_7_out, and_8_out, and_9_out,
       and_10_out, and_11_out, and_12_out, and_13_out, and_14_out, and_15_out, and_16_out, and_17_out,
       and_18_out, and_19_out, and_20_out, and_21_out, and_22_out, and_23_out, clock_1_out;
  wire [2:0] or_3_out, register_1_q;

  or or_1 (or_3_out[2], and_1_out, and_2_out, and_3_out);
  or or_2 (or_3_out[1], and_4_out, and_5_out, and_6_out);
  or or_3 (or_3_out[0], and_7_out, and_8_out, and_9_out);
  and and_1 (and_1_out, register_1_q[2], ~a);  // AND_Gate
  and and_2 (and_2_out, a, ~register_1_q[1]);  // AND_Gate
  and and_3 (and_3_out, register_1_q[1], register_1_q[0], a);
  and and_4 (and_4_out, ~register_1_q[2], register_1_q[1], ~register_1_q[0]);  // AND_Gate
  and and_5 (and_5_out, register_1_q[1], ~a);  // AND_Gate
  and and_6 (and_6_out, ~register_1_q[1], register_1_q[0], a);  // AND_Gate
  and and_7 (and_7_out, ~register_1_q[1], ~register_1_q[0], a);  // AND_Gate
  and and_8 (and_8_out, ~a, ~register_1_q[0], a);  // AND_Gate
  and and_9 (and_9_out, register_1_q[0], ~a);  // AND_Gate
  Register #(.width(3)) register_1 (.D(or_3_out), .Q(register_1_q), .clk(clock_1_out));  // open: en, clr
  Clock clock_1 (.out(clock_1_out));
  and and_10 (and_10_out, register_1_q[1], ~register_1_q[0], ~a);  // AND_Gate
  and and_11 (and_11_out, register_1_q[2], ~register_1_q[1], a);  // AND_Gate
  and and_12 (and_12_out, ~register_1_q[1], register_1_q[0], a);  // AND_Gate
  and and_13 (and_13_out, register_1_q[2], register_1_q[0]);
  and and_14 (and_14_out, ~register_1_q[2], register_1_q[1], ~register_1_q[0]);  // AND_Gate
  and and_15 (and_15_out, ~register_1_q[2], ~register_1_q[0], a);  // AND_Gate
  and and_16 (and_16_out, ~register_1_q[2], ~register_1_q[1], a);  // AND_Gate
  and and_17 (and_17_out, ~register_1_q[2], register_1_q[0], ~a);  // AND_Gate
  and and_18 (and_18_out, ~register_1_q[2], register_1_q[1], ~register_1_q[0], ~a);  // AND_Gate
  and and_19 (and_19_out, register_1_q[2], ~register_1_q[1], ~register_1_q[0]);  // AND_Gate
  and and_20 (and_20_out, ~register_1_q[2], ~register_1_q[1], a);  // AND_Gate
  and and_21 (and_21_out, ~register_1_q[2], register_1_q[0], a);  // AND_Gate
  and and_22 (and_22_out, ~register_1_q[2], ~register_1_q[1], register_1_q[0]);  // AND_Gate
  and and_23 (and_23_out, register_1_q[2], register_1_q[0], ~a);  // AND_Gate
  or or_4 (x, and_10_out, and_11_out, and_12_out, and_13_out);
  or or_5 (y, and_14_out, and_15_out, and_16_out, and_17_out);
  or or_6 (z, and_18_out, and_19_out, and_20_out, and_21_out, and_22_out, and_23_out);
endmodule
